// Logisim project Practical-10-3 Bit Ripple Counter.circ as structural Verilog: 1 circuit, main circuit main
module main (
  input  in_1,
  output out_2,
  output out_3,
  output out_4
);

  wire clock_1_out;

  J_K_Flip_Flop j_k_ff_1 (.J(in_1), .clk(out_3), .K(in_1), .Q(out_2));  // open: Qn, preset, en, reset
  J_K_Flip_Flop j_k_ff_2 (.J(in_1), .clk(out_4), .K(in_1), .Q(out_3));  // open: Qn, preset, en, reset
  Clock clock_1 (.out(clock_1_out));
  J_K_Flip_Flop j_k_ff_3 (.J(in_1), .clk(clock_1_out), .K(in_1), .Q(out_4));  // open: Qn, preset, en, reset

  // Notes on the sheet:
  //   3 Bit Ripple Counter
  //   Practical 10
endmodule
