// Logisim project Practical-6.1-JK  FF.circ as structural Verilog: 1 circuit, main circuit main
module main (
  input  J,
  input  K,
  input  in_3,
  input  in_4,
  output Q,
  output Q_prime,
  output out_7
);

  wire and_1_out, and_2_out, CLK_out, clock_1_out, nand_1_out, nand_2_out, not_1_out, or_1_out;

  and and_1 (and_1_out, J, Q_prime);
  and and_2 (and_2_out, K, Q);
  or or_1 (or_1_out, and_1_out, and_2_out);
  Clock CLK (.out(CLK_out));
  not not_1 (not_1_out, or_1_out);
  Clock clock_1 (.out(clock_1_out));
  nand nand_1 (nand_1_out, or_1_out, CLK_out);
  nand nand_2 (nand_2_out, CLK_out, not_1_out);
  J_K_Flip_Flop j_k_ff_1 (.J(in_3), .clk(clock_1_out), .K(in_4), .Q(out_7));  // open: Qn, preset, en, reset
  nand nand_3 (Q, nand_1_out, Q_prime);
  nand nand_4 (Q_prime, Q, nand_2_out);

  // Notes on the sheet:
  //   JK Flip Flop
  //   Practical 6
endmodule
