// Logisim project Practical-6.2-D  FF.circ as structural Verilog: 1 circuit, main circuit main
module main (
  input  in_1,
  input  D,
  output out_3,
  output Q,
  output Q_prime
);

  wire CLK_out, clock_1_out, nand_1_out, nand_2_out, not_1_out;

  Clock CLK (.out(CLK_out));
  not not_1 (not_1_out, D);
  nand nand_1 (nand_1_out, D, CLK_out);
  nand nand_2 (nand_2_out, CLK_out, not_1_out);
  Clock clock_1 (.out(clock_1_out));
  D_Flip_Flop d_ff_1 (.clk(clock_1_out), .D(in_1), .Q(out_3));  // open: Qn, preset, en, reset
  nand nand_3 (Q, nand_1_out, Q_prime);
  nand nand_4 (Q_prime, Q, nand_2_out);

  // Notes on the sheet:
  //   D Flip Flop
  //   Practical 6
endmodule
