// Logisim project Practical-6.3-SR FF.circ as structural Verilog: 1 circuit, main circuit main
module main (
  input  S__SET,
  input  R__RESET,
  output out_3,
  output out_4
);

  nand nand_1 (out_3, S__SET, out_4);
  nand nand_2 (out_4, out_3, R__RESET);

  // Notes on the sheet:
  //   SR FLIP FLOP
endmodule
