// Logisim project Practical-7-Counter.circ as structural Verilog: 1 circuit, main circuit main
module main (
  input  in_1,
  input  in_2,
  output out_3,
  output out_4
);

  wire and_1_out, clock_1_out, clock_2_out, j_k_ff_1_q, j_k_ff_2_q, t_ff_1_q;

  Clock clock_1 (.out(clock_1_out));
  Clock clock_2 (.out(clock_2_out));
  T_Flip_Flop t_ff_1 (.clk(clock_1_out), .T(in_1), .Q(t_ff_1_q));  // open: Qn, preset, reset, en
  J_K_Flip_Flop j_k_ff_1 (.J(in_2), .clk(clock_2_out), .K(in_2), .Q(j_k_ff_1_q));  // open: Qn, preset, en, reset
  T_Flip_Flop t_ff_2 (.clk(t_ff_1_q), .T(in_1), .Q(out_3));  // open: Qn, preset, reset, en
  J_K_Flip_Flop j_k_ff_2 (
    .J(j_k_ff_1_q), .clk(clock_2_out), .K(j_k_ff_1_q), .Q(j_k_ff_2_q));  // open: Qn, preset, en, reset
  and and_1 (and_1_out, j_k_ff_1_q, j_k_ff_2_q);
  J_K_Flip_Flop j_k_ff_3 (.J(and_1_out), .clk(clock_2_out), .K(and_1_out), .Q(out_4));  // open: Qn, preset, en, reset

  // Notes on the sheet:
  //   2 Bit Asynchronous Ripple Counter
  //   2 Bit Synchronous Ripple Counter
  //   Practical 7
endmodule
