// Logisim project Practical-8.1-4 bit shift Register SISO.circ as structural Verilog: 1 circuit, main circuit main
module main (
  input  Serial_Input,
  output Serial_Output
);

  wire clock_1_out, d_ff_1_q, d_ff_2_q, d_ff_3_q;

  Clock clock_1 (.out(clock_1_out));
  D_Flip_Flop d_ff_1 (.clk(clock_1_out), .D(Serial_Input), .Q(d_ff_1_q));  // open: Qn, preset, en, reset
  D_Flip_Flop d_ff_2 (.clk(clock_1_out), .D(d_ff_1_q), .Q(d_ff_2_q));  // open: Qn, preset, en, reset
  D_Flip_Flop d_ff_3 (.clk(clock_1_out), .D(d_ff_2_q), .Q(d_ff_3_q));  // open: Qn, preset, en, reset
  D_Flip_Flop d_ff_4 (.clk(clock_1_out), .D(d_ff_3_q), .Q(Serial_Output));  // open: Qn, preset, en, reset

  // Notes on the sheet:
  //   Serial In Serial Out
  //   Practical 8
endmodule
