// Logisim project Practical-8.2-4 bit shift Register PIPO.circ as structural Verilog: 1 circuit, main circuit main
module main (
  input  Parallel_Input,
  input  PI,
  input  PI_2,
  input  PI_3,
  output Parallel_Output,
  output PO,
  output PO_2,
  output PO_3
);

  wire clock_1_out;

  Clock clock_1 (.out(clock_1_out));
  D_Flip_Flop d_ff_1 (.clk(clock_1_out), .D(Parallel_Input), .Q(PO), .en(clock_1_out));  // open: Qn, preset, reset
  D_Flip_Flop d_ff_2 (.clk(clock_1_out), .D(PI), .Q(PO_2), .en(clock_1_out));  // open: Qn, preset, reset
  D_Flip_Flop d_ff_3 (.clk(clock_1_out), .D(PI_2), .Q(PO_3), .en(clock_1_out));  // open: Qn, preset, reset
  D_Flip_Flop d_ff_4 (.clk(clock_1_out), .D(PI_3), .Q(Parallel_Output), .en(clock_1_out));  // open: Qn, preset, reset

  // Notes on the sheet:
  //   Parallel In Parallel Out
  //   Practical 8
endmodule
