// Logisim project Practical-8.3-4 bit shift Register SIPO.circ as structural Verilog: 1 circuit, main circuit main
module main (
  input  Parallel_Input,
  output Parallel_Output,
  output PO,
  output PO_2,
  output PO_3
);

  wire clock_1_out;

  Clock clock_1 (.out(clock_1_out));
  D_Flip_Flop d_ff_1 (.clk(clock_1_out), .D(Parallel_Input), .Q(PO));  // open: Qn, preset, en, reset
  D_Flip_Flop d_ff_2 (.clk(clock_1_out), .D(PO), .Q(PO_2));  // open: Qn, preset, en, reset
  D_Flip_Flop d_ff_3 (.clk(clock_1_out), .D(PO_2), .Q(PO_3));  // open: Qn, preset, en, reset
  D_Flip_Flop d_ff_4 (.clk(clock_1_out), .D(PO_3), .Q(Parallel_Output));  // open: Qn, preset, en, reset

  // Notes on the sheet:
  //   Serial In Parallel Out
  //   Practical 8
endmodule
