// Logisim project Practical-9.2-DEMUX.circ as structural Verilog: 1 circuit, main circuit main
// Y3
module main (
  input  D,
  input  S1,
  input  S0,
  output Y3,
  output Y2,
  output Y2_2,
  output Y0
);

  wire not_1_out, not_2_out;

  not not_1 (not_1_out, S0);
  not not_2 (not_2_out, S1);
  and and_1 (Y3, S1, S0, D);
  and and_2 (Y2, S1, not_1_out, D);
  and and_3 (Y2_2, not_2_out, S1, D);
  and and_4 (Y0, not_2_out, not_1_out, D);

  // Notes on the sheet:
  //   1:4 Demultiplexer
  //   Practical 9
endmodule
