// Logisim project Practical-4.1-Binary to Gray convertor.circ as structural Verilog: 1 circuit, main circuit main
module main (
  input  B3,
  input  B2,
  input  B1,
  input  B0,
  output g3,
  output g2,
  output g1,
  output g0
);

  xor xor_1 (g2, B3, B2);
  xor xor_2 (g1, B2, B1);
  xor xor_3 (g0, B1, B0);

  assign g3 = B3;

  // Notes on the sheet:
  //   Binary to Gray code Convertor
  //   Practical 4.1
endmodule
