// Logisim project Practical-4.2- Gray to Binary convertor.circ as structural Verilog: 1 circuit, main circuit main
module main (
  input  g3,
  input  g2,
  input  g1,
  input  g0,
  output B3,
  output B2,
  output B1,
  output B0
);

  xor xor_1 (B2, g3, g2);
  xor xor_2 (B1, B2, g1);
  xor xor_3 (B0, B1, g0);

  assign B3 = g3;

  // Notes on the sheet:
  //   Gray to Binary code Convertor
  //   Practical 4.2
endmodule
