// Logisim project Practical-5.3-Half Subtractor.circ as structural Verilog: 1 circuit, main circuit main
module main (
  input  A,
  input  B,
  output D,
  output B_2
);

  wire not_1_out;

  not not_1 (not_1_out, A);
  xor xor_1 (D, A, B);
  and and_1 (B_2, B, not_1_out);

  // Notes on the sheet:
  //   Half Subtractor
  //   Practical 5.3
endmodule
