// Logisim project Practical-5.4-Half Adder.circ as structural Verilog: 1 circuit, main circuit main
module main (
  input  Half_Adder,
  input  in_2,
  output out_3,
  output out_4
);

  xor xor_1 (out_3, Half_Adder, in_2);
  and and_1 (out_4, in_2, Half_Adder);

  // Notes on the sheet:
  //   Practical 5.1
endmodule
