// Logisim project Practical-7.1-MUX 4.1.circ as structural Verilog: 1 circuit, main circuit main
module main (
  input  S1,
  input  S0,
  input  in_3,
  input  in_4,
  input  in_5,
  input  in_6,
  output out_7
);

  wire and_1_out, and_2_out, and_3_out, and_4_out, not_1_out, not_2_out;

  not not_1 (not_1_out, S0);
  not not_2 (not_2_out, S1);
  and and_1 (and_1_out, S1, S0, in_3);
  and and_2 (and_2_out, S1, not_1_out, in_4);
  and and_3 (and_3_out, not_2_out, S1, in_5);
  and and_4 (and_4_out, not_2_out, not_1_out, in_6);
  or or_1 (out_7, and_1_out, and_2_out, and_3_out, and_4_out);

  // Notes on the sheet:
  //   4:1 Multiplexer
  //   Practical 9
endmodule
