// Logisim project JK  FF.circ as structural Verilog: 1 circuit, main circuit main
module main (
  input  D,
  input  D_2,
  output Q,
  output Q_prime
);

  wire and_1_out, and_2_out, CLK_out, nand_1_out, nand_2_out, not_1_out, or_1_out;

  and and_1 (and_1_out, D, Q_prime);
  and and_2 (and_2_out, D_2, ~Q);  // AND_Gate
  or or_1 (or_1_out, and_1_out, and_2_out);
  Clock CLK (.out(CLK_out));
  not not_1 (not_1_out, or_1_out);
  nand nand_1 (nand_1_out, or_1_out, CLK_out);
  nand nand_2 (nand_2_out, CLK_out, not_1_out);
  nand nand_3 (Q, nand_1_out, Q_prime);
  nand nand_4 (Q_prime, Q, nand_2_out);
endmodule
